# Fritzing sketch LCD mini breadboard soldered (saved by Fritzing 1.0.4)
stripboards: 2

parts:
  J1 = female pin header, 16 pins [form="♀ (female)"]
  J2 = female pin header, 2 pins [form="♀ (female)"]
  J3 = male pin header, 2 pins [form="♂ (male)"]
  J4 = male pin header, 6 pins [form="♂ (male)"]  # not connected
  J5 = male pin header, 6 pins [form="♂ (male)"]
  J6 = female pin header, 16 pins [form="♀ (female)"]
  J7 = female pin header, 2 pins [form="♀ (female)"]
  J8 = male pin header, 2 pins [form="♂ (male)"]
  R1 = TRIMPOT [maximum_resistance=10kΩ knob_status=50% power=0.5W package=3362u-2]
  R2 = Resistor [tolerance=±5% power=0.25W resistance=330 package=THT]
  R3 = Resistor [tolerance=±5% power=0.25W resistance=330 package=THT]
  U1 = LCD-16X2 [package=lcd-16x2_noholes]

nets:
  N1: J1.pin1, J1.pin16, J2.pin1, J3.pin1, U1.VSS, U1.K
  N2: J1.pin2, U1.VDD
  N3: J1.pin3, U1.VO
  N4: J1.pin4, U1.RS
  N5: J1.pin5, U1.R_W
  N6: J1.pin6, U1.E
  N7: J1.pin7, U1.DB0
  N8: J1.pin8, U1.DB1
  N9: J1.pin9, U1.DB2
  N10: J1.pin10, U1.DB3
  N11: J1.pin11, U1.DB4
  N12: J1.pin12, U1.DB5
  N13: J1.pin13, U1.DB6
  N14: J1.pin14, U1.DB7
  N15: J1.pin15, R2.Pin_0, U1.A
  N16: J2.pin2, J3.pin2, R2.Pin_1
  N17: J5.pin1, J5.pin2, J6.pin3, J6.pin4
  N18: J5.pin3, J6.pin5
  N19: J5.pin4, J6.pin6
  N20: J5.pin5, J6.pin11
  N21: J5.pin6, J6.pin13
  N22: J6.pin1, J6.pin12, J6.pin16, J7.pin2, J8.pin2, R1.CCW
  N23: J6.pin2, R3.Pin_1
  N24: J6.pin14, R1.WIPER
  N25: J6.pin15, J7.pin1, J8.pin1, R1.CW, R3.Pin_0
