# Fritzing sketch arduino basic lab instrument (saved by Fritzing 0.9.10b)
breadboards: 2

parts:
  U1 = LCD-16X2 [package=lcd-16x2_noholes]
  Part1 = Arduino Uno (Rev3) - ICSP
  R1 = TRIMPOT [maximum_resistance=10kΩ knob_status=50% power=0.5W package=3362u-2]
  S2 = Tactile Switch Buttons - 12mm Square [package=tactile-pth-12mm]
  S3 = Tactile Switch Buttons - 12mm Square [package=tactile-pth-12mm]
  S4 = Tactile Switch Buttons - 12mm Square [package=tactile-pth-12mm]
  S5 = Tactile Switch Buttons - 12mm Square [package=tactile-pth-12mm]
  R2 = Resistor [tolerance=±5% resistance=330 package="0805 [SMD]"]
  R3 = Resistor [tolerance=±5% resistance=330 package="0402 [SMD]"]
  S6 = Toggle Switch [package=THT]
  LED1 = LED - 5mm [color="Green (570nm)" current=0.030 package="5 mm [THT]"]

nets:
  VSS: U1.VSS, U1.R_W, U1.K, Part1.GND, R1.CCW, S2.1, S2.3, S3.1, S3.3, S4.1, S4.3, S5.1, S5.3, R2.Pin_1, S6.L2
  VDD: U1.VDD, Part1.5V, R1.CW, R3.Pin_0
  N1: U1.VO, R1.WIPER
  N2: U1.RS, Part1.D2
  N3: U1.E, Part1.D3_PWM
  N4: U1.DB4, Part1.D4
  N5: U1.DB5, Part1.D5_PWM
  N6: U1.DB6, Part1.D6_PWM
  N7: U1.DB7, Part1.D7
  N8: U1.A, R3.Pin_1
  N9: Part1.A0, S2.2, S2.4
  N10: Part1.A1, S3.2, S3.4
  N11: Part1.A2, S4.2, S4.4
  N12: Part1.A3, S5.2, S5.4
  N13: Part1.A5/SCL, S6.COM
  N14: Part1.D13/SCK, LED1.anode
  N15: R2.Pin_0, LED1.cathode

custom parts:
  Tactile Switch Buttons - 12mm Square: Medium-sized clicky momentary switches are standard input "buttons" on electronic projects. These work best in a PCB but can be used on a solderless breadboard as shown in this tutorial. The pins are normally open (disconnected) and when the button is pressed they are momentarily closed. They come in a pack of 10, they're pretty handy so you'll want to keep them around. You can find an EAGLE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
