# Fritzing sketch mini switch panel soldered (saved by Fritzing 1.0.4)
perfboards: 2

parts:
  S1 = Tactile switch 12mm [package=THT]
  S2 = Tactile switch 12mm [package=THT]
  S3 = Tactile switch 12mm [package=THT]
  S4 = Tactile switch 12mm [package=THT]
  J1 = rounded female pin header, 2 pins [form="♀ (female rounded)"]  # not connected
  J2 = female pin header, 9 pins [form="♀ (female)"]
  J3 = female pin header, 6 pins [form="♀ (female)"]
  J4 = female pin header, 6 pins [form="♀ (female)"]
  J5 = female pin header, 6 pins [form="♀ (female)"]
  J6 = rounded female pin header, 2 pins [form="♀ (female rounded)"]
  J7 = female pin header, 6 pins [form="♀ (female)"]  # not connected
  J8 = female pin header, 6 pins [form="♀ (female)"]  # not connected
  J9 = female pin header, 6 pins [form="♀ (female)"]  # not connected
  J10 = female pin header, 9 pins [form="♀ (female)"]
  R1 = Resistor [tolerance=±5% resistance=330 package="0603 [SMD]"]
  S6 = Tactile switch 12mm [package=THT]
  S8 = Tactile switch 12mm [package=THT]
  S5 = Tactile switch 12mm [package=THT]
  S7 = Tactile switch 12mm [package=THT]

nets:
  N1: S1.1, S1.2
  N2: S1.3, S1.4
  N3: S2.1, S2.2
  N4: S2.3, S2.4
  N5: S3.1, S3.2
  N6: S3.3, S3.4
  N7: S4.1, S4.2
  N8: S4.3, S4.4
  N9: J2.pin1, J3.pin1
  N10: J2.pin2, J3.pin2
  N11: J2.pin3, J3.pin3
  N12: J2.pin4, J3.pin4
  N13: J2.pin5, J3.pin5
  N14: J2.pin6, J3.pin6
  N15: J2.pin7, J5.pin6
  N16: J2.pin8, J4.pin6
  N17: J6.pin1, J10.pin2, S6.1, S6.2, S8.1, S8.2, S5.1, S5.2, S7.1, S7.2
  N18: J6.pin2, R1.Pin_0
  N19: S6.3, S6.4
  N20: S8.3, S8.4
  N21: S5.3, S5.4
  N22: S7.3, S7.4

custom parts:
  Tactile switch 12mm: 12 mm tactile switch (push button/momentary switch) from the B3F family.
  Tactile switch 12mm: 12 mm tactile switch (push button/momentary switch) from the B3F family.
  Tactile switch 12mm: 12 mm tactile switch (push button/momentary switch) from the B3F family.
  Tactile switch 12mm: 12 mm tactile switch (push button/momentary switch) from the B3F family.
