# Fritzing sketch monochromator stepper motor shield (saved by Fritzing 1.0.4)

parts:
  Part1 = Adafruit Proto Shield R3 [part_number="Adafruit #2077"]
  U1 = JST XH 3A Male [chip_label=? package=THT]
  U2 = JST XH 4A 2.54mm [package=THT]
  DRV_1 = DRV 8825 Stepper Motor Carrier, High Current [part_number="DRV 8825"]  # not connected
  J1 = Screw terminal - 2 pins [package=THT]
  C1 = Capacitor Polarized [package=cpol-radial-100uf-25v]

nets:
  N1: Part1.1#0, Part1.P$5#1, Part1.VIN, Part1.N$84, J1.pin2, C1.+
  N2: Part1.GND, Part1.1#123, Part1.1#163, Part1.P$5#164, Part1.1#166, Part1.P$5#167, Part1.N$17, Part1.N$83, J1.pin1, C1.-
  N3: Part1.A4, Part1.N$150
  N4: Part1.1#129, Part1.N$210
  N5: Part1.1#132, Part1.N$214
  N6: Part1.D12, Part1.1#193, Part1.P$5#194
  N7: Part1.D11, Part1.1#172, Part1.P$5#173
  N8: Part1.D10, Part1.N$115, Part1.P$5#161
  N9: Part1.D9, Part1.P$5#181
  N10: Part1.D8, Part1.P$5#197
  N11: Part1.N$126, U1.pin1
  N12: Part1.P$5#184, Part1.P$5#200, Part1.+5V
  N13: Part1.1#202, Part1.N$23
  N14: Part1.1#205, Part1.N$215
  N15: Part1.N$9, U1.pin2
  N16: Part1.N$10, U1.pin3
  N17: Part1.N$114, U2.pin1
  N18: Part1.N$118, U2.pin2
  N19: Part1.N$119, U2.pin3
  N20: Part1.N$123, U2.pin4

custom parts:
  Adafruit Proto Shield R3: This prototyping shield is the best out there (well, we think so, at least), and now is even better with Version R3 - updated for the most compatibility with just about all the Arduinos! It works with UNO, Mega, Leonardo, NG, Diecimila, Duemilanove, and compatible Arduinos. Yun's and Arduino Ethernets have a chunky Ethernet jack that gets in the way of stacking, you can use the stacking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
  JST XH 3A Male: 2.54 Mm JST "XH" connector
  JST XH 4A 2.54mm: 4 Pin JST XH connector
